// Logisim project ALUControl-ControlUnit.circ as structural Verilog: 2 circuits, main circuit ALu control unit
module ALu_control_unit (
  input  f0,
  input  f1,
  input  f2,
  input  f3,
  input  f4,
  input  f5,
  input  OP0,
  input  OP1,
  input  OP2,
  output jr,
  output Binv,
  output AluCon2,
  output AluCon1,
  output AluCon0
);

  wire addiu_out, addu_out, beq_bne_out, lw_out, nor_out, or_out, ori_out, slt_out, Xori_out;

  and u_jr (jr, ~f0, ~f1, ~f2, f3, ~f4, ~f5, OP0, OP1, ~OP2);  // AND_Gate
  and beq_bne (beq_bne_out, OP0, ~OP1, ~OP2);  // AND_Gate
  and slt (slt_out, ~f0, f1, ~f2, f3, ~f4, f5, OP0, OP1, ~OP2);  // AND_Gate
  and \or  (or_out, f0, ~f1, f2, ~f3, ~f4, f5, OP0, OP1, ~OP2);  // AND_Gate
  // AND_Gate and has open pins: in0=f0, in1=f1, in2=f2, in3=f3, in4=f4, in5=f5, in6=OP0, in7=OP1, in8=OP2, out=open
  and subu (Binv, f0, f1, ~f2, ~f3, ~f4, f5, OP0, OP1, ~OP2);  // AND_Gate
  and addu (addu_out, f0, ~f1, ~f2, ~f3, ~f4, f5, OP0, OP1, ~OP2);  // AND_Gate
  and \nor  (nor_out, f0, f1, f2, ~f3, ~f4, f5, OP0, OP1, ~OP2);  // AND_Gate
  and lw (lw_out, ~OP0, ~OP1, ~OP2);  // AND_Gate
  and ori (ori_out, ~OP0, OP1, ~OP2);  // AND_Gate
  // AND_Gate andi has open pins: in0=OP0, in1=OP1, in2=OP2, out=open
  and addiu (addiu_out, OP0, ~OP1, OP2);  // AND_Gate
  and Xori (Xori_out, ~OP0, OP1, OP2);  // AND_Gate
  or or_2 (AluCon2, nor_out, beq_bne_out, slt_out, Xori_out);
  or or_3 (AluCon1, addu_out, lw_out, addiu_out, Binv, slt_out);
  or or_4 (AluCon0, ori_out, nor_out, or_out);
endmodule

module controlUnit (
  input  OP0,
  input  OP1,
  input  OP2,
  input  OP3,
  input  OP4,
  input  OP5,
  output RegDst0,
  output RegDst1,
  output Jump,
  output Branch,
  output MemRead,
  output MemtoReg,
  output MemWrite,
  output Alusrc,
  output RegWrite,
  output ExtOp1,
  output OP0_2,
  output OP1_2,
  output OP2_2,
  output what_write1,
  output what_write0,
  output beq_bne
);

  wire addiu_out, andi_out, bne_out, j_out, ori_out, Xori_out;

  and r_type (RegDst0, ~OP5, ~OP4, ~OP3, ~OP2, ~OP1, ~OP0);  // AND_Gate
  and lw (MemRead, OP5, ~OP4, ~OP3, ~OP2, OP1, OP0);  // AND_Gate
  and sw (MemWrite, OP5, ~OP4, OP3, ~OP2, OP1, OP0);  // AND_Gate
  and beq (beq_bne, ~OP5, ~OP4, ~OP3, OP2, ~OP1, ~OP0);  // AND_Gate
  and j (j_out, ~OP5, ~OP4, ~OP3, ~OP2, OP1, ~OP0);  // AND_Gate
  and ori (ori_out, ~OP5, ~OP4, OP3, OP2, ~OP1, OP0);  // AND_Gate
  and andi (andi_out, ~OP5, ~OP4, OP3, OP2, ~OP1, ~OP0);  // AND_Gate
  and addiu (addiu_out, ~OP5, ~OP4, OP3, ~OP2, ~OP1, OP0);  // AND_Gate
  and bne (bne_out, ~OP5, ~OP4, ~OP3, OP2, ~OP1, OP0);  // AND_Gate
  and Xori (Xori_out, ~OP5, ~OP4, OP3, OP2, OP1, ~OP0);  // AND_Gate
  and jal (RegDst1, ~OP5, ~OP4, ~OP3, ~OP2, OP1, OP0);  // AND_Gate
  and Lui (what_write0, ~OP5, ~OP4, OP3, OP2, OP1, OP0);  // AND_Gate
  or or_1 (Branch, bne_out, beq_bne);
  or or_2 (Alusrc, Xori_out, addiu_out, andi_out, MemWrite, MemRead, ori_out);
  or or_3 (RegWrite, ori_out, Xori_out, addiu_out, andi_out, RegDst0, MemRead, what_write0, RegDst1);
  or or_4 (ExtOp1, andi_out, Xori_out, addiu_out, ori_out);
  or or_5 (OP1_2, Xori_out, RegDst0, ori_out);
  or or_6 (OP2_2, andi_out, addiu_out, Xori_out);
  or or_7 (Jump, j_out, RegDst1);
  or or_8 (OP0_2, addiu_out, RegDst0, beq_bne, bne_out);

  assign MemtoReg = MemRead;
  assign what_write1 = RegDst1;
endmodule
