// Logisim project Alu.circ as structural Verilog: 1 circuit, main circuit main
module main (
  input  B_inver,
  input  [31:0] in_2,
  input  [2:0] Selection,
  input  [31:0] in_4,
  output [31:0] out_5,
  output out_6,
  output Zero
);

  wire [0:0] comparator_1_lt;
  wire [31:0] adder_1_out, and_1_out, multiplexer_1_out, nor_1_out, not_1_out, or_1_out, xor_1_out;

  assign not_1_out = ~in_4;  // NOT_Gate not_1, 32 bits wide
  Multiplexer #(.width(32)) multiplexer_1 (
    .in0(in_4), .in1(not_1_out), .out(multiplexer_1_out), .sel(B_inver));  // open: en
  Adder #(.width(32)) adder_1 (.a(in_2), .b(multiplexer_1_out), .out(adder_1_out), .cin(B_inver), .cout(out_6));
  assign or_1_out = in_2 | in_4;  // OR_Gate or_1, 32 bits wide
  assign xor_1_out = in_2 ^ in_4;  // XOR_Gate xor_1, 32 bits wide
  assign nor_1_out = ~(in_2 | in_4);  // NOR_Gate nor_1, 32 bits wide
  Comparator #(.width(32)) comparator_1 (.a(in_2), .b(in_4), .eq(Zero), .lt(comparator_1_lt[0]));  // open: gt
  assign and_1_out = in_2 & in_4;  // AND_Gate and_1, 32 bits wide
  Multiplexer #(.select(3), .width(32)) multiplexer_2 (
    .in0(and_1_out), .in1(or_1_out), .in2(adder_1_out), .in4(xor_1_out), .in5(nor_1_out),
    .in6({{31{1'b0}}, comparator_1_lt[0]}), .out(out_5), .sel(Selection));  // open: in3, in7, en

  // Notes on the sheet:
  //   A
  //   B
  //   output
endmodule
