// Logisim project Extintion-Shift.circ as structural Verilog: 7 circuits, main circuit s2l
module s2l (
  input  [31:0] \input ,
  output [31:0] \output 
);


  assign \output  = {\input [29:0], 2'b00};
endmodule

module _0extended (
  input  [15:0] \input ,
  output [31:0] \output 
);


  assign \output  = {{16{1'b0}}, \input };
endmodule

module _1extended (
  input  [15:0] \input ,
  output [31:0] \output 
);


  assign \output  = {{16{1'b1}}, \input };
endmodule

module signExtended (
  input  [15:0] \input ,
  output [31:0] \output 
);


  assign \output  = {{17{\input [15]}}, \input [14:0]};
endmodule

module s2l26bit (
  input  [25:0] in_1,
  output [27:0] out_2
);


  assign out_2 = {in_1, 2'b00};
endmodule

module _0ex_in_begin (
  input  [15:0] \input ,
  output [31:0] \output 
);


  assign \output  = {\input , {16{1'b0}}};
endmodule

module sltex (
  input  \input ,
  output [31:0] \output 
);


  assign \output  = {{31{1'b0}}, \input };
endmodule
