// Logisim project Project.circ as structural Verilog: 1 circuit, main circuit main
module main (
);

  wire alu_control_unit_1_binv, and_1_out, button_1_out, Clock, controlunit_1_alusrc, controlunit_1_beq_bne,
       controlunit_1_branch, controlunit_1_extop1, controlunit_1_memread, controlunit_1_memtoreg,
       controlunit_1_memwrite, controlunit_1_regwrite, led_1_p1, main_1_zero, multiplexer_7_out, not_1_out,
       or_1_out;
  wire [1:0] alu_control_unit_1_jr, controlunit_1_regdst0, controlunit_1_what_write0;
  wire [2:0] alu_control_unit_1_alucon0, controlunit_1_op0_2;
  wire [4:0] multiplexer_2_out;
  wire [5:0] mipsprogramrom_1_p2;
  wire [25:0] mipsprogramrom_1_p2_2;
  wire [27:0] shift_2_to_left_2_out_2;
  wire [31:0] adder_1_out, adder_2_out, main_1_out_5, multiplexer_1_out, multiplexer_3_out,
       multiplexer_4_out, multiplexer_6_out, multiplexer_8_out, n0ex_in_begin_1_output, PC_q, ram_1_data,
       registerfile_1_p1, registerfile_1_p7, registerfile_1_p8, shift_2_to_left_output, signExt_output,
       zeroExt_output;

  Register #(.width(32)) PC (.D(multiplexer_3_out), .en(1'b1), .Q(PC_q), .clk(Clock), .clr(button_1_out));
  Button button_1 (.out(button_1_out));
  Clock clock_1 (.out(Clock));
  s2l shift_2_to_left (.\input (signExt_output), .\output (shift_2_to_left_output));
  Adder #(.width(32)) adder_1 (.a(32'h4), .b(PC_q), .out(adder_1_out));  // open: cin, cout
  s2l26bit shift_2_to_left_2 (.in_1(mipsprogramrom_1_p2_2), .out_2(shift_2_to_left_2_out_2));
  // MIPSProgramROM mipsprogramrom_1: pin names not known; wires that end beside it: PC_q, {mipsprogramrom_1_p2, mipsprogramrom_1_p2_2}
  ROM rom_1 ();  // open: addr, data, sel
  Adder #(.width(32)) adder_2 (.a(shift_2_to_left_output), .b(adder_1_out), .out(adder_2_out));  // open: cin, cout
  controlUnit controlunit_1 (
    .OP0(mipsprogramrom_1_p2[0]), .OP1(mipsprogramrom_1_p2[1]), .OP2(mipsprogramrom_1_p2[2]),
    .OP3(mipsprogramrom_1_p2[3]), .OP4(mipsprogramrom_1_p2[4]), .OP5(mipsprogramrom_1_p2[5]),
    .RegDst0(controlunit_1_regdst0[0]), .RegDst1(controlunit_1_regdst0[1]), .Jump(alu_control_unit_1_jr[1]),
    .Branch(controlunit_1_branch), .MemRead(controlunit_1_memread), .MemtoReg(controlunit_1_memtoreg),
    .MemWrite(controlunit_1_memwrite), .Alusrc(controlunit_1_alusrc), .RegWrite(controlunit_1_regwrite),
    .ExtOp1(controlunit_1_extop1), .OP0_2(controlunit_1_op0_2[0]), .OP1_2(controlunit_1_op0_2[1]),
    .OP2_2(controlunit_1_op0_2[2]), .what_write1(controlunit_1_what_write0[1]),
    .what_write0(controlunit_1_what_write0[0]), .beq_bne(controlunit_1_beq_bne));
  Multiplexer #(.width(32), .enable("false")) multiplexer_1 (
    .in0(adder_1_out), .in1(adder_2_out), .out(multiplexer_1_out), .sel(and_1_out));
  Multiplexer #(.select(2), .width(5), .enable("false")) multiplexer_2 (
    .in0(mipsprogramrom_1_p2_2[20:16]), .in1(mipsprogramrom_1_p2_2[15:11]), .in2({5{1'b1}}),
    .out(multiplexer_2_out), .sel(controlunit_1_regdst0));  // open: in3
  signExtended signExt (.\input (mipsprogramrom_1_p2_2[15:0]), .\output (signExt_output));
  _0extended zeroExt (.\input (mipsprogramrom_1_p2_2[15:0]), .\output (zeroExt_output));
  Multiplexer #(.select(2), .width(32), .enable("false")) multiplexer_3 (
    .in0(multiplexer_1_out), .in1(registerfile_1_p7), .in2({adder_1_out[31:28], shift_2_to_left_2_out_2}),
    .out(multiplexer_3_out), .sel(alu_control_unit_1_jr));  // open: in3
  // RegisterFile registerfile_1: pin names not known; wires that end beside it: registerfile_1_p1, Clock, controlunit_1_regwrite, multiplexer_2_out, mipsprogramrom_1_p2_2[25:21], mipsprogramrom_1_p2_2[20:16], registerfile_1_p7, registerfile_1_p8
  Multiplexer #(.width(32), .enable("false")) multiplexer_4 (
    .in0(signExt_output), .in1(zeroExt_output), .out(multiplexer_4_out), .sel(controlunit_1_extop1));
  Multiplexer #(.select(2), .width(32), .enable("false")) multiplexer_5 (
    .in0(multiplexer_8_out), .in1(n0ex_in_begin_1_output), .in2(adder_1_out), .out(registerfile_1_p1),
    .sel(controlunit_1_what_write0));  // open: in3
  Multiplexer #(.width(32), .enable("false")) multiplexer_6 (
    .in0(registerfile_1_p8), .in1(multiplexer_4_out), .out(multiplexer_6_out), .sel(controlunit_1_alusrc));
  _0ex_in_begin u_0ex_in_begin_1 (.\input (mipsprogramrom_1_p2_2[15:0]), .\output (n0ex_in_begin_1_output));
  and and_1 (and_1_out, controlunit_1_branch, multiplexer_7_out);
  Multiplexer #(.enable("false")) multiplexer_7 (
    .in0(not_1_out), .in1(main_1_zero), .out(multiplexer_7_out), .sel(controlunit_1_beq_bne));
  not not_1 (not_1_out, main_1_zero);
  // LED led_1: pin names not known; wires that end beside it: led_1_p1
  ALU_main main_1 (
    .B_inver(alu_control_unit_1_binv), .in_2(registerfile_1_p7), .Selection(alu_control_unit_1_alucon0),
    .in_4(multiplexer_6_out), .out_5(main_1_out_5), .out_6(led_1_p1), .Zero(main_1_zero));
  ALu_control_unit alu_control_unit_1 (
    .f0(mipsprogramrom_1_p2_2[0]), .f1(mipsprogramrom_1_p2_2[1]), .f2(mipsprogramrom_1_p2_2[2]),
    .f3(mipsprogramrom_1_p2_2[3]), .f4(mipsprogramrom_1_p2_2[4]), .f5(mipsprogramrom_1_p2_2[5]),
    .OP0(controlunit_1_op0_2[0]), .OP1(controlunit_1_op0_2[1]), .OP2(controlunit_1_op0_2[2]),
    .jr(alu_control_unit_1_jr[0]), .Binv(alu_control_unit_1_binv), .AluCon2(alu_control_unit_1_alucon0[2]),
    .AluCon1(alu_control_unit_1_alucon0[1]), .AluCon0(alu_control_unit_1_alucon0[0]));
  or or_1 (or_1_out, controlunit_1_memwrite, controlunit_1_memread);
  RAM #(.addrWidth(24), .dataWidth(32), .bus("separate")) ram_1 (
    .addr(main_1_out_5[23:0]), .din(registerfile_1_p8), .data(ram_1_data), .str(controlunit_1_memwrite),
    .sel(or_1_out), .clk(Clock), .ld(controlunit_1_memread), .clr(1'b0));
  Multiplexer #(.width(32), .enable("false")) multiplexer_8 (
    .in0(main_1_out_5), .in1(ram_1_data), .out(multiplexer_8_out), .sel(controlunit_1_memtoreg));

  // Notes on the sheet:
  //   contents of rom_1 (hex, n*v repeats v):
  //   0 0 0 1 0 10 0 10 1 4*0 10 5*0 1 0 10 0 10 1 4*0 10 1
endmodule
